// Logisim project CPU_Design_1.circ as structural Verilog: 5 circuits, main circuit main
module main (
  input  [15:0] Data_Bus,
  input  in_2
);

  wire [15:0] undriven;

  Operation_Type_Decoder Operation_Decoder (.Input_Data(Data_Bus));  // open: Op_Type
  Selector Register ();  // open: Input_Data, CLK, Register_Select, Output_Data
  ROM #(.addrWidth(16), .dataWidth(16)) rom_1 (.addr(undriven), .sel(in_2));  // open: data
endmodule

module Selector (
  input  CLK,
  input  [15:0] Input_Data,
  input  [2:0] Register_Select,
  output [15:0] Output_Data
);

  wire [15:0] demultiplexer_1_out1, demultiplexer_1_out2, demultiplexer_1_out3, demultiplexer_1_out4,
       demultiplexer_1_out5, demultiplexer_1_out6, demultiplexer_1_out7, X0_q, X1_q, X2_q, X3_q, X4_q, X5_q,
       X6_q, X7_q;

  Demultiplexer #(.select(3), .width(16), .enable("false")) demultiplexer_1 (
    .out1(demultiplexer_1_out1), .out2(demultiplexer_1_out2), .out3(demultiplexer_1_out3),
    .out4(demultiplexer_1_out4), .out5(demultiplexer_1_out5), .out6(demultiplexer_1_out6),
    .out7(demultiplexer_1_out7), .in(Input_Data), .sel(Register_Select));  // open: out0
  Register #(.width(16)) X0 (.D(16'h1), .Q(X0_q), .clk(CLK));  // open: en, clr
  Register #(.width(16)) X1 (.D(demultiplexer_1_out1), .Q(X1_q));  // open: en, clk, clr
  Register #(.width(16)) X2 (.D(demultiplexer_1_out2), .Q(X2_q), .clk(CLK));  // open: en, clr
  Register #(.width(16)) X3 (.D(demultiplexer_1_out3), .Q(X3_q), .clk(CLK));  // open: en, clr
  Register #(.width(16)) X4 (.D(demultiplexer_1_out4), .Q(X4_q), .clk(CLK));  // open: en, clr
  Register #(.width(16)) X5 (.D(demultiplexer_1_out5), .Q(X5_q), .clk(CLK));  // open: en, clr
  Register #(.width(16)) X6 (.D(demultiplexer_1_out6), .Q(X6_q), .clk(CLK));  // open: en, clr
  Register #(.width(16)) X7 (.D(demultiplexer_1_out7), .Q(X7_q), .clk(CLK));  // open: en, clr
  Multiplexer #(.select(3), .width(16), .enable("false")) multiplexer_1 (
    .in0(X0_q), .in1(X1_q), .in2(X2_q), .in3(X3_q), .in4(X4_q), .in5(X5_q), .in6(X6_q), .in7(X7_q),
    .out(Output_Data), .sel(Register_Select));
endmodule

module ALU (
  input  [15:0] Rs1,
  input  [15:0] Rs2,
  input  [3:0] op_select,
  output Negative_Bit,
  output Zero_Bit,
  output [15:0] Rd
);

  wire [3:0] undriven;
  wire [15:0] adder_1_out, and_1_out, divider_1_out, divider_1_rem, multiplier_1_out, nand_1_out, nor_1_out,
       not_1_out, or_1_out, shifter_1_out, shifter_2_out, shifter_3_out, shifter_4_out, shifter_5_out,
       subtractor_1_out, xor_1_out;

  Adder #(.width(16)) adder_1 (.a(Rs1), .b(Rs2), .out(adder_1_out));  // open: cin, cout
  Subtractor #(.width(16)) subtractor_1 (.a(Rs1), .b(Rs2), .out(subtractor_1_out), .bin(1'b0));  // open: bout
  Multiplier #(.width(16)) multiplier_1 (.a(Rs1), .b(Rs2), .out(multiplier_1_out));  // open: cin, cout
  Divider #(.width(16)) divider_1 (.a(Rs1), .b(Rs2), .out(divider_1_out), .rem(divider_1_rem));  // open: upper
  Shifter #(.width(16)) shifter_1 (.in(Rs1), .\dist (undriven), .out(shifter_1_out));
  Shifter #(.width(16), .shift("lr")) shifter_2 (.in(Rs1), .\dist (undriven), .out(shifter_2_out));
  Shifter #(.width(16), .shift("ar")) shifter_3 (.in(Rs1), .\dist (undriven), .out(shifter_3_out));
  Shifter #(.width(16), .shift("rl")) shifter_4 (.in(Rs1), .\dist (undriven), .out(shifter_4_out));
  Shifter #(.width(16), .shift("rr")) shifter_5 (.in(Rs1), .\dist (undriven), .out(shifter_5_out));
  assign and_1_out = Rs1 & Rs2;  // AND_Gate and_1, 16 bits wide
  assign or_1_out = Rs1 | Rs2;  // OR_Gate or_1, 16 bits wide
  assign xor_1_out = Rs1 ^ Rs2;  // XOR_Gate xor_1, 16 bits wide
  assign nand_1_out = ~(Rs1 & Rs2);  // NAND_Gate nand_1, 16 bits wide
  assign nor_1_out = ~(Rs1 | Rs2);  // NOR_Gate nor_1, 16 bits wide
  assign not_1_out = ~Rs1;  // NOT_Gate not_1, 16 bits wide
  Multiplexer #(.select(4), .width(16), .enable("false")) multiplexer_1 (
    .in0(adder_1_out), .in1(subtractor_1_out), .in2(multiplier_1_out), .in3(divider_1_out),
    .in4(divider_1_rem), .in5(and_1_out), .in6(or_1_out), .in7(xor_1_out), .in8(nand_1_out), .in9(nor_1_out),
    .in10(not_1_out), .in11(shifter_1_out), .in12(shifter_2_out), .in13(shifter_3_out), .in14(shifter_4_out),
    .in15(shifter_5_out), .out({Rd[15:1], Negative_Bit}), .sel(op_select));
  nor nor_2 (Zero_Bit, Negative_Bit, Rd[1], Rd[2], Rd[3], Rd[4], Rd[5], Rd[6], Rd[7], Rd[9], Rd[10], Rd[11], Rd[12], Rd[13], Rd[14], Rd[15], Rd[8]);

  assign Rd[0] = Negative_Bit;
endmodule

module Operation_Type_Decoder (
  input  [15:0] Input_Data,
  output [3:0] Op_Type
);

  nor nor_1 (Op_Type[0], Input_Data[2], Input_Data[3], Input_Data[4]);
  and and_1 (Op_Type[1], Input_Data[2], ~Input_Data[3], ~Input_Data[4]);  // AND_Gate
  and and_2 (Op_Type[2], Input_Data[2], Input_Data[3], Input_Data[4]);

  // Notes on the sheet:
  //   0 = R-Type   1 = CBZ   2 = BR
endmodule

module Data_Seter (
  input  [3:0] Op_Type
);
endmodule
